# Fritzing sketch scheme-nano-L293D (saved by Fritzing 0.9.10b)
breadboards: 1

parts:
  IC1 = L293D [package=THT]
  Componente1 = Arduino Nano (Rev3.0)
  M2 = DC Motor [voltage_(max)=6V voltage_(min)=3V]
  M3 = DC Motor [voltage_(max)=6V voltage_(min)=3V]
  6xAA_Battery1 = 6xAA Battery
  LED1 = smd LED [color="Red (633nm)" package="0805 [SMD]"]
  R1 = Resistor [tolerance=±5% resistance=220 package="2512 [SMD]"]
  HC-SR04_Sensor_1 = HC-SR04 Ultrasonic Distance Sensor

nets:
  5V: IC1.Enable_1, IC1.+Vmotor, IC1.Enable_2, IC1.+V, Componente1.VIN, 6xAA_Battery1.Pin_2, R1.Pin_1
  N1: IC1.In_1, Componente1.D5
  N2: IC1.Out_1_(_Controlled_by_Enable_1_), M2.pin_2
  GND: IC1.0V, Componente1.GND, 6xAA_Battery1.Pin_1, LED1.cathode, HC-SR04_Sensor_1.GND
  N3: IC1.Out_2_(_Controlled_by_Enable_1_), M2.pin_1
  N4: IC1.In_2, Componente1.D6
  N5: IC1.In_3, Componente1.D7
  N6: IC1.Out_3_(_Controlled_by_Enable_2_), M3.pin_2
  N7: IC1.Out_4_(_Controlled_by_Enable_2_), M3.pin_1
  N8: IC1.In_4, Componente1.D8
  5V_2: Componente1.5V, HC-SR04_Sensor_1.VCC
  N9: Componente1.A5, HC-SR04_Sensor_1.TRIG
  N10: Componente1.A4, HC-SR04_Sensor_1.ECHO
  N11: LED1.anode, R1.Pin_0

custom parts:
  6xAA Battery: 6xAA battery
